# Fritzing sketch Untitled Sketch (saved by Fritzing 0.8.7b)
breadboards: 1

parts:
  Componente1 = Arduino Mega 2560 (Rev3)
  T1 = LM35 Temperature Sensor [package="TO92 [THT]"]
  J1 = Piezo Speaker

nets:
  N1: Componente1.A0, T1.Vout
  GND: Componente1.GND, T1.GND, J1.pin1
  N2: Componente1.D11_PWM, J1.pin2
  N3: Componente1.5V, T1.+Vs
